// Logisim project processor_riscv2(1).circ as structural Verilog: 6 circuits, main circuit main
module main (
  input  [2:0] F,
  input  in_2,
  input  [31:0] A,
  input  [31:0] B,
  output [31:0] Y
);

  wire comparator_1_lt;
  wire [31:0] adder_1_out, and_1_out, bit_extender_1_out, multiplexer_1_out, not_1_out, or_1_out;

  assign not_1_out = ~B;  // NOT_Gate not_1, 32 bits wide
  Multiplexer #(.width(32), .enable("false")) multiplexer_1 (
    .in0(B), .in1(not_1_out), .out(multiplexer_1_out), .sel(F[0]));
  Adder #(.width(32)) adder_1 (.a(A), .b(multiplexer_1_out), .out(adder_1_out), .cin(F[0]));  // open: cout
  assign and_1_out = A & B;  // AND_Gate and_1, 32 bits wide
  assign or_1_out = A | B;  // OR_Gate or_1, 32 bits wide
  Comparator #(.width(32), .mode("unsigned")) comparator_1 (
    .a(A), .b(adder_1_out), .lt(comparator_1_lt));  // open: gt, eq
  assign bit_extender_1_out = {{31{1'b0}}, comparator_1_lt};  // Bit_Extender bit_extender_1
  Multiplexer #(.select(3), .width(32), .enable("false")) multiplexer_2 (
    .in0(adder_1_out), .in1(adder_1_out), .in2(and_1_out), .in3(or_1_out), .in4(or_1_out),
    .in5(bit_extender_1_out), .out(Y), .sel(F));  // open: in6, in7
  Comparator #(.width(32), .mode("unsigned")) comparator_2 (.a(Y), .b({32{1'b0}}), .eq(in_2));  // open: gt, lt

  // Notes on the sheet:
  //   ALUcontroll
  //   F[0]
  //   A & B
  //   add/subs
  //   A | B
  //   A < B
  //   Zero Extends
  //   F[2:0]
  //   set less then if A<B = 1 else 0
  //   if all bits Resultat Y = 0 then zero = 1 
  //   Results
  //   Zero
endmodule

module ALU (
  input  [2:0] F,
  input  [31:0] A,
  input  [31:0] B,
  output out_4,
  output [31:0] Y
);

  wire comparator_1_lt;
  wire [31:0] adder_1_out, and_1_out, bit_extender_1_out, multiplexer_1_out, multiplier_1_out, not_1_out,
       or_1_out;

  assign not_1_out = ~B;  // NOT_Gate not_1, 32 bits wide
  Multiplexer #(.width(32), .enable("false")) multiplexer_1 (
    .in0(B), .in1(not_1_out), .out(multiplexer_1_out), .sel(F[0]));
  Adder #(.width(32)) adder_1 (.a(A), .b(multiplexer_1_out), .out(adder_1_out), .cin(F[0]));  // open: cout
  assign and_1_out = A & B;  // AND_Gate and_1, 32 bits wide
  assign or_1_out = A | B;  // OR_Gate or_1, 32 bits wide
  Comparator #(.width(32), .mode("unsigned")) comparator_1 (
    .a(A), .b(adder_1_out), .lt(comparator_1_lt));  // open: gt, eq
  Multiplier #(.width(32)) multiplier_1 (.a(B), .b(A), .out(multiplier_1_out));  // open: cin, cout
  assign bit_extender_1_out = {{31{1'b0}}, comparator_1_lt};  // Bit_Extender bit_extender_1
  Multiplexer #(.select(3), .width(32), .enable("false")) multiplexer_2 (
    .in0(adder_1_out), .in1(adder_1_out), .in2(and_1_out), .in3(or_1_out), .in4(multiplier_1_out),
    .in5(bit_extender_1_out), .out(Y), .sel(F));  // open: in6, in7
  Comparator #(.width(32), .mode("unsigned")) comparator_2 (.a(Y), .b({32{1'b0}}), .eq(out_4));  // open: gt, lt

  // Notes on the sheet:
  //   ALUcontroll
  //   F[0]
  //   A & B
  //   add/subs
  //   A | B
  //   A < B
  //   Zero Extends
  //   F[2:0]
  //   set less then if A<B = 1 else 0
  //   if all bits Resultat Y = 0 then zero = 1 
  //   Results
  //   Zero
endmodule

module Datapath (
  output [7:0] Next_Address,
  output [31:0] Data_Memmory,
  output [31:0] t2
);

  wire alu_1_out_4, and_1_out, clock_1_out, controlunit_1_alusrc, controlunit_1_branch,
       controlunit_1_regwrite;
  wire [2:0] controlunit_1_alucontrol;
  wire [7:0] adder_1_out, adder_2_out, bit_extender_2_out, register_1_q, shifter_1_out;
  wire [31:0] bit_extender_1_out, multiplexer_2_out, registerfile_1_rd1, registerfile_1_rd2, rom_1_data;

  Multiplexer #(.width(8), .enable("false")) multiplexer_1 (
    .in0(adder_1_out), .in1(adder_2_out), .out(Next_Address), .sel(and_1_out));
  Clock clock_1 (.out(clock_1_out));
  Register register_1 (.D(Next_Address), .Q(register_1_q), .clk(clock_1_out));  // open: en, clr
  Adder adder_1 (.a(register_1_q), .b(8'h4), .out(adder_1_out));  // open: cin, cout
  Shifter #(.shift("lr")) shifter_1 (.in(register_1_q), .\dist (3'b010), .out(shifter_1_out));
  ROM #(.dataWidth(32)) rom_1 (.addr(shifter_1_out), .data(rom_1_data));  // open: sel
  RegisterFile registerfile_1 (
    .CLK(clock_1_out), .A1(rom_1_data[17:15]), .WD3(Data_Memmory), .A2(rom_1_data[22:20]),
    .WE3(controlunit_1_regwrite), .RD1(registerfile_1_rd1), .RD2(registerfile_1_rd2), .A3(rom_1_data[9:7]),
    .T2(t2));
  assign bit_extender_1_out = {{20{rom_1_data[31]}}, rom_1_data[31:20]};  // Bit_Extender bit_extender_1
  Bit_Extender #(.in_width(13), .out_width(8), .\type ("sign")) bit_extender_2 (
    .in({rom_1_data[31], rom_1_data[7], rom_1_data[30:25], rom_1_data[11:8], 1'b0}), .out(bit_extender_2_out));
  Multiplexer #(.width(32), .enable("false")) multiplexer_2 (
    .in0(registerfile_1_rd2), .in1(bit_extender_1_out), .out(multiplexer_2_out), .sel(controlunit_1_alusrc));
  ControlUnit controlunit_1 (
    .Instruction(rom_1_data), .RegWrite(controlunit_1_regwrite), .ALUSrc(controlunit_1_alusrc),
    .ALUControl(controlunit_1_alucontrol), .Branch(controlunit_1_branch));
  and and_1 (and_1_out, controlunit_1_branch, alu_1_out_4);
  ALU alu_1 (
    .F(controlunit_1_alucontrol), .out_4(alu_1_out_4), .A(registerfile_1_rd1), .Y(Data_Memmory),
    .B(multiplexer_2_out));
  Adder adder_2 (.a(register_1_q), .b(bit_extender_2_out), .out(adder_2_out));  // open: cin, cout

  // Notes on the sheet:
  //   contents of rom_1 (hex, n*v repeats v):
  //   800293 100393 28863 25383b3 fff28293 fe000ae3 63
endmodule

module RegisterFile (
  input  CLK,
  input  [2:0] A1,
  input  [31:0] WD3,
  input  [2:0] A2,
  input  WE3,
  input  [2:0] A3,
  output [31:0] RD1,
  output [31:0] RD2,
  output [31:0] T2
);

  wire and_1_out, and_2_out, and_3_out, and_4_out, and_5_out, and_6_out, and_7_out, decoder_1_out1,
       decoder_1_out2, decoder_1_out3, decoder_1_out4, decoder_1_out5, decoder_1_out6, decoder_1_out7;
  wire [31:0] register_1_q, register_2_q, register_3_q, register_4_q, register_5_q, register_6_q, zero_q;

  Decoder #(.select(3)) decoder_1 (
    .out1(decoder_1_out1), .out2(decoder_1_out2), .out3(decoder_1_out3), .out4(decoder_1_out4),
    .out5(decoder_1_out5), .out6(decoder_1_out6), .out7(decoder_1_out7), .sel(A3));  // open: out0, en
  and and_1 (and_1_out, WE3, decoder_1_out1);
  and and_2 (and_2_out, WE3, decoder_1_out2);
  and and_3 (and_3_out, WE3, decoder_1_out3);
  and and_4 (and_4_out, WE3, decoder_1_out4);
  and and_5 (and_5_out, WE3, decoder_1_out5);
  and and_6 (and_6_out, WE3, decoder_1_out6);
  and and_7 (and_7_out, WE3, decoder_1_out7);
  Register #(.width(32)) zero (.D({32{1'b0}}), .Q(zero_q), .clk(CLK));  // open: en, clr
  Register #(.width(32)) register_1 (.D(WD3), .en(and_1_out), .Q(register_1_q), .clk(CLK));  // open: clr
  Register #(.width(32)) register_2 (.D(WD3), .en(and_2_out), .Q(register_2_q), .clk(CLK));  // open: clr
  Register #(.width(32)) register_3 (.D(WD3), .en(and_3_out), .Q(register_3_q), .clk(CLK));  // open: clr
  Register #(.width(32)) register_4 (.D(WD3), .en(and_4_out), .Q(register_4_q), .clk(CLK));  // open: clr
  Register #(.width(32)) register_5 (.D(WD3), .en(and_5_out), .Q(register_5_q), .clk(CLK));  // open: clr
  Register #(.width(32)) register_6 (.D(WD3), .en(and_6_out), .Q(register_6_q), .clk(CLK));  // open: clr
  Register #(.width(32)) register_7 (.D(WD3), .en(and_7_out), .Q(T2), .clk(CLK));  // open: clr
  Multiplexer #(.select(3), .width(32)) multiplexer_1 (
    .in0(zero_q), .in1(register_1_q), .in2(register_2_q), .in3(register_3_q), .in4(register_4_q),
    .in5(register_5_q), .in6(register_6_q), .in7(T2), .out(RD1), .sel(A1));  // open: en
  Multiplexer #(.select(3), .width(32)) multiplexer_2 (
    .in0(zero_q), .in1(register_1_q), .in2(register_2_q), .in3(register_3_q), .in4(register_4_q),
    .in5(register_5_q), .in6(register_6_q), .in7(T2), .out(RD2), .sel(A2));  // open: en
endmodule

module ControlUnit (
  input  [31:0] Instruction,
  output RegWrite,
  output ALUSrc,
  output [2:0] ALUControl,
  output Branch
);

  wire and_1_out, comparator_3_eq, comparator_4_eq;
  wire [1:1] or_2_out;
  wire [2:0] multiplexer_1_out;

  Comparator #(.width(7), .mode("unsigned")) comparator_1 (
    .a(Instruction[6:0]), .b(7'b1100011), .eq(Branch));  // open: gt, lt
  Comparator #(.width(7), .mode("unsigned")) comparator_2 (
    .a(Instruction[6:0]), .b(7'b0010011), .eq(ALUSrc));  // open: gt, lt
  Comparator #(.width(7), .mode("unsigned")) comparator_3 (
    .a(Instruction[6:0]), .b(7'b0110011), .eq(comparator_3_eq));  // open: gt, lt
  Comparator #(.width(7), .mode("unsigned")) comparator_4 (
    .a(Instruction[31:25]), .b(7'b0000001), .eq(comparator_4_eq));  // open: gt, lt
  and and_1 (and_1_out, comparator_3_eq, comparator_4_eq);
  or or_1 (RegWrite, ALUSrc, comparator_3_eq);
  or or_2 (or_2_out[1], ALUSrc, comparator_3_eq);
  Multiplexer #(.select(2), .width(3), .enable("false")) multiplexer_1 (
    .in0(3'b000), .in1(3'b001), .in2(3'b000), .in3(3'b000), .out(multiplexer_1_out),
    .sel({or_2_out[1], Branch}));
  Multiplexer #(.width(3), .enable("false")) multiplexer_2 (
    .in0(multiplexer_1_out), .in1(3'b100), .out(ALUControl), .sel(and_1_out));

  // Notes on the sheet:
  //   branch
  //   addi
  //   add
  //   addi | add
endmodule

module Tests (
  output [31:0] Y,
  output [3:0] Y_2,
  output [7:0] Y_3
);


  assign Y = 32'hf4010207;
  assign Y_2 = 4'b0010;
  assign Y_3 = 8'h22;

  // Notes on the sheet:
  //   binary values in Logisim. Convince yourself how the bits are displayed.
  //   Example 1: A simple example that illustrates how 32-bit values are displayed as 
  //   Example 2) An example of how to extra certain bits from a (in this case) 32-bit wire. Here we extract the bits 8..11 from the 32-bit wire.
  //   Example 3) Sometimes it is useful to extra bits from different position and the re-assemble them. In this case, we extract bits 8..11 and bits 15..18 and assemble them into an 8-bit wire.
endmodule
