// Logisim project processor_riscv_surprise.circ as structural Verilog
module ALU (
  input  [2:0] F,
  input  [31:0] B,
  input  [31:0] A,
  output [2:0] SELECT,
  output [31:0] Y,
  output ZERO
);

  wire comparator_1_gt;
  wire [31:0] adder_1_out, AND_out, bit_extender_1_out, multiplexer_1_out, multiplier_1_out, NOT_out, OR_out;

  assign NOT_out = ~B;  // NOT_Gate NOT, 32 bits wide
  Multiplexer #(.width(32), .enable("false")) multiplexer_1 (
    .in0(B), .in1(NOT_out), .out(multiplexer_1_out), .sel(F[0]));
  Adder #(.width(32)) adder_1 (.a(multiplexer_1_out), .b(A), .out(adder_1_out), .cin(F[0]));  // open: cout
  assign AND_out = B & A;  // AND_Gate AND, 32 bits wide
  assign OR_out = B | A;  // OR_Gate OR, 32 bits wide
  assign bit_extender_1_out = {{31{1'b0}}, comparator_1_gt};  // Bit_Extender bit_extender_1
  Comparator #(.width(32), .mode("unsigned")) comparator_1 (.a(B), .b(A), .gt(comparator_1_gt));  // open: eq, lt
  Multiplier #(.width(32)) multiplier_1 (.a(B), .b(A), .out(multiplier_1_out));  // open: cin, cout
  Multiplexer #(.select(3), .width(32), .enable("false")) multiplexer_2 (
    .in0(adder_1_out), .in1(adder_1_out), .in2(AND_out), .in3(OR_out), .in4(multiplier_1_out),
    .in5(bit_extender_1_out), .out(Y), .sel(F));  // open: in6, in7
  Comparator #(.width(32), .mode("unsigned")) comparator_2 (.a(Y), .b({32{1'b0}}), .eq(ZERO));  // open: gt, lt

  assign SELECT = F;

  // Notes on the sheet:
  //   A-B = A +(NOT B + 1)
endmodule

module Datapath (
  output ALUSrc,
  output [2:0] F,
  output Branch_AND_Zero,
  output [31:0] A,
  output [31:0] B,
  output [31:0] t2
);

  wire alu_1_zero, clock_1_out, controlunit_1_branch, controlunit_1_regwrite;
  wire [7:0] adder_1_out, adder_2_out, bit_extender_1_out, multiplexer_1_out, multiplexer_2_out,
       register_1_q, shifter_1_out;
  wire [31:0] alu_1_y, bit_extender_2_out, registerfile_1_rd2, rom_1_data;

  Clock clock_1 (.out(clock_1_out));
  Multiplexer #(.width(8), .enable("false")) multiplexer_1 (
    .in0(adder_1_out), .in1(adder_2_out), .out(multiplexer_1_out), .sel(Branch_AND_Zero));
  Register register_1 (.D(multiplexer_1_out), .Q(register_1_q), .clk(clock_1_out));  // open: en, clr
  Adder adder_1 (.a(register_1_q), .b(8'h4), .out(adder_1_out));  // open: cin, cout
  Shifter #(.shift("lr")) shifter_1 (.in(register_1_q), .\dist (3'b010), .out(shifter_1_out));
  Multiplexer #(.width(8), .enable("false")) multiplexer_2 (
    .in0(adder_1_out), .in1(register_1_q), .out(multiplexer_2_out), .sel(Branch_AND_Zero));
  ROM #(.dataWidth(32)) rom_1 (.addr(shifter_1_out), .data(rom_1_data));  // open: sel
  Bit_Extender #(.in_width(13), .out_width(8), .\type ("sign")) bit_extender_1 (
    .in({rom_1_data[31], rom_1_data[7], rom_1_data[30:25], rom_1_data[11:8], 1'b0}), .out(bit_extender_1_out));
  RegisterFile registerfile_1 (
    .CLK(clock_1_out), .A1(rom_1_data[17:15]), .WD3(alu_1_y), .A2(rom_1_data[22:20]),
    .WE3(controlunit_1_regwrite), .RD1(A), .RD2(registerfile_1_rd2), .A3(rom_1_data[9:7]), .T2(t2));
  assign bit_extender_2_out = {{20{rom_1_data[31]}}, rom_1_data[31:20]};  // Bit_Extender bit_extender_2
  ControlUnit controlunit_1 (
    .Instruction(rom_1_data), .RegWrite(controlunit_1_regwrite), .ALUSrc(ALUSrc), .ALUControl(F),
    .Branch(controlunit_1_branch));
  Multiplexer #(.width(32), .enable("false")) multiplexer_3 (
    .in0(registerfile_1_rd2), .in1(bit_extender_2_out), .out(B), .sel(ALUSrc));
  ALU alu_1 (.F(F), .B(B), .A(A), .Y(alu_1_y), .ZERO(alu_1_zero));  // open: SELECT
  Adder adder_2 (.a(multiplexer_2_out), .b(bit_extender_1_out), .out(adder_2_out));  // open: cin, cout
  and and_1 (Branch_AND_Zero, controlunit_1_branch, alu_1_zero);

  // Notes on the sheet:
  //   PC +=4
  //   contents of rom_1 (hex, n*v repeats v):
  //   400293 100393 100193 28c63 328a63 328863 118193 23383b3 fe000ae3 63
  //   PC + B_imm
endmodule

module RegisterFile (
  input  CLK,
  input  [2:0] A1,
  input  [31:0] WD3,
  input  [2:0] A2,
  input  WE3,
  input  [2:0] A3,
  output [31:0] RD1,
  output [31:0] RD2,
  output [31:0] T2
);

  wire and_1_out, and_2_out, and_3_out, and_4_out, and_5_out, and_6_out, and_7_out, and_8_out,
       decoder_1_out0, decoder_1_out1, decoder_1_out2, decoder_1_out3, decoder_1_out4, decoder_1_out5,
       decoder_1_out6, decoder_1_out7;
  wire [31:0] gp_q, ra_q, sp_q, t0_q, t1_q, tp_q, zero_q;

  Decoder #(.select(3)) decoder_1 (
    .out0(decoder_1_out0), .out1(decoder_1_out1), .out2(decoder_1_out2), .out3(decoder_1_out3),
    .out4(decoder_1_out4), .out5(decoder_1_out5), .out6(decoder_1_out6), .out7(decoder_1_out7), .sel(A3));  // open: en
  and and_1 (and_1_out, WE3, decoder_1_out0);
  and and_2 (and_2_out, WE3, decoder_1_out1);
  and and_3 (and_3_out, WE3, decoder_1_out2);
  and and_4 (and_4_out, WE3, decoder_1_out3);
  and and_5 (and_5_out, WE3, decoder_1_out4);
  and and_6 (and_6_out, WE3, decoder_1_out5);
  and and_7 (and_7_out, WE3, decoder_1_out6);
  and and_8 (and_8_out, WE3, decoder_1_out7);
  Register #(.width(32)) zero (.D({32{1'b0}}), .en(and_1_out), .Q(zero_q), .clk(CLK));  // open: clr
  Register #(.width(32)) ra (.D(WD3), .en(and_2_out), .Q(ra_q), .clk(CLK));  // open: clr
  Register #(.width(32)) sp (.D(WD3), .en(and_3_out), .Q(sp_q), .clk(CLK));  // open: clr
  Register #(.width(32)) gp (.D(WD3), .en(and_4_out), .Q(gp_q), .clk(CLK));  // open: clr
  Register #(.width(32)) tp (.D(WD3), .en(and_5_out), .Q(tp_q), .clk(CLK));  // open: clr
  Register #(.width(32)) t0 (.D(WD3), .en(and_6_out), .Q(t0_q), .clk(CLK));  // open: clr
  Register #(.width(32)) t1 (.D(WD3), .en(and_7_out), .Q(t1_q), .clk(CLK));  // open: clr
  Register #(.width(32)) u_t2 (.D(WD3), .en(and_8_out), .Q(T2), .clk(CLK));  // open: clr
  Multiplexer #(.select(3), .width(32)) multiplexer_1 (
    .in0(zero_q), .in1(ra_q), .in2(sp_q), .in3(gp_q), .in4(tp_q), .in5(t0_q), .in6(t1_q), .in7(T2),
    .out(RD1), .sel(A1));  // open: en
  Multiplexer #(.select(3), .width(32)) multiplexer_2 (
    .in0(zero_q), .in1(ra_q), .in2(sp_q), .in3(gp_q), .in4(tp_q), .in5(t0_q), .in6(t1_q), .in7(T2),
    .out(RD2), .sel(A2));  // open: en
endmodule

module ControlUnit (
  input  [31:0] Instruction,
  output [2:0] ALUControl,
  output Branch,
  output RegWrite,
  output ALUSrc
);

  wire and_1_out, comparator_1_eq, comparator_4_eq;
  wire [2:0] multiplexer_1_out;
  wire [6:0] bit_extender_1_out;

  assign bit_extender_1_out = {{3{1'b0}}, Instruction[15:12]};  // Bit_Extender bit_extender_1
  Comparator #(.width(7), .mode("unsigned")) comparator_1 (
    .a(7'b0001000), .b(bit_extender_1_out), .eq(comparator_1_eq));  // open: gt, lt
  Comparator #(.width(7), .mode("unsigned")) comparator_2 (
    .a(Instruction[6:0]), .b(7'b1100011), .eq(Branch));  // open: gt, lt
  Comparator #(.width(7), .mode("unsigned")) comparator_3 (
    .a(Instruction[6:0]), .b(7'b0010011), .eq(ALUSrc));  // open: gt, lt
  Comparator #(.width(7), .mode("unsigned")) comparator_4 (
    .a(Instruction[6:0]), .b(7'b0110011), .eq(comparator_4_eq));  // open: gt, lt
  and and_1 (and_1_out, comparator_1_eq, comparator_4_eq);
  Multiplexer #(.width(3), .enable("false")) multiplexer_1 (
    .in0(3'b000), .in1(3'b001), .out(multiplexer_1_out), .sel(Branch));
  or or_1 (RegWrite, ALUSrc, comparator_4_eq);
  Multiplexer #(.width(3), .enable("false")) multiplexer_2 (
    .in0(multiplexer_1_out), .in1(3'b100), .out(ALUControl), .sel(and_1_out));

  // Notes on the sheet:
  //   branch
  //   I-type
  //   R-type
  //   Add
  //   Sub
endmodule

module Tests (
  output [31:0] Y,
  output [3:0] Y_2,
  output [7:0] Y_3
);


  assign Y = 32'hf4010207;
  assign Y_2 = 4'b0010;
  assign Y_3 = 8'h22;

  // Notes on the sheet:
  //   binary values in Logisim. Convince yourself how the bits are displayed.
  //   Example 1: A simple example that illustrates how 32-bit values are displayed as 
  //   Example 2) An example of how to extra certain bits from a (in this case) 32-bit wire. Here we extract the bits 8..11 from the 32-bit wire.
  //   Example 3) Sometimes it is useful to extra bits from different position and the re-assemble them. In this case, we extract bits 8..11 and bits 15..18 and assemble them into an 8-bit wire.
endmodule

module ALU_Test (
  input  [2:0] in_1,
  output [31:0] OUTPUT
);

  wire alu_1_zero;

  ALU alu_1 (.F(in_1), .B(32'h1), .A(32'h9), .Y(OUTPUT), .ZERO(alu_1_zero));  // open: SELECT
  LED ZERO (.in(alu_1_zero));
endmodule
